# Fritzing sketch blinkLed_pushButton (saved by Fritzing 0.9.3b)
breadboards: 1

parts:
  Composant1 = Arduino Uno (Rev3)
  LED1 = LED - 5mm [color="Red (633nm)" package="5 mm [THT]"]
  R1 = Resistor [tolerance=±5% resistance=220 package=THT]
  LED2 = LED - 5mm [color="Green (565nm)" package="5 mm [THT]"]
  R2 = Resistor [tolerance=±5% resistance=220 package=THT]
  S1 = Pushbutton [package="[THT]"]
  R3 = Resistor [tolerance=±5% resistance=220 package=THT]

nets:
  N1: Composant1.D11_PWM/MOSI, R2.Pin_0
  N2: Composant1.D12/MISO, R1.Pin_0
  N3: Composant1.5V, S1.Pin_3, S1.Pin_4
  N4: Composant1.GND, LED1.cathode, LED2.cathode, R3.Pin_1
  N5: LED1.anode, R1.Pin_1
  N6: LED2.anode, R2.Pin_1
  N7: S1.Pin_1, S1.Pin_2, R3.Pin_0

// code stored in the sketch: BlinkWithoutDelay_2ndLED.ino
const int buttonPin_2 = 2;
const int ledPin_11 = 11;
const int ledPin_12 = 12;

int ledState = LOW;

unsigned long previousMillis = 0;

const long interval = 1000;

void setup() {

  pinMode(ledPin_11, OUTPUT);
  pinMode(ledPin_12, OUTPUT);
  pinMode(buttonPin_2, INPUT);
}

void loop() {

  unsigned long currentMillis = millis();

  if (currentMillis - previousMillis >= interval) {

    previousMillis = currentMillis;

    if (ledState == LOW) {
      ledState = HIGH;
    } else {
      ledState = LOW;
    }

    digitalWrite(ledPin_11, ledState);
  }

  int state = digitalRead(buttonPin_2);
  if(state)
    digitalWrite(ledPin_12, HIGH);
  else
    digitalWrite(ledPin_12, LOW);
  
}

// code stored in the sketch: FeuRouge.ino
int red1 = 3;
int orange1 = 4;
int green1 = 5;
int red2 = 6;
int orange2 = 7;
int green2 = 8;
int i , flag = HIGH ;

void setup() {                
for (i = 3; i <= 8 ; ++i)
	pinMode(i, OUTPUT); 	
}

void loop() {
  digitalWrite(red1, LOW);
  digitalWrite(green2, LOW);
  digitalWrite(orange1, HIGH);  
  digitalWrite(green1, HIGH); 
  digitalWrite(red2, HIGH); 
  digitalWrite(orange2, HIGH);
  delay(20000);
  digitalWrite(green2, HIGH);
  for (i = 0; i < 10; ++i)
  {	
  	flag = !flag ;
  	digitalWrite(orange2, flag);
            delay(500);
  }
  digitalWrite(red1, HIGH);
  digitalWrite(orange2, HIGH);
  digitalWrite(red2 , LOW);
  digitalWrite(green1 , LOW);
  delay(20000);
  digitalWrite(green1 , HIGH);
  for (i = 0; i < 10; ++i)
  {	
  	flag = !flag ;
  	digitalWrite(orange1, flag);
            delay(500);
  }
}
